# Fritzing sketch Pathfinder (saved by Fritzing 0.9.3b)
breadboards: 1

parts:
  Nokia_5110_LCD_Module1 = Nokia5110LCDModule
  U1 = ESP8266 WiFi Module [part_number=ESP8266]
  GY-NEO6MV3 = SUP500F [package=sup500f]
  Gyroscope = Triple Axis Accelerometer Breakout - ADXL335
  Composant2 = Arduino Uno (Rev3)
  VCC1 = Battery

nets:
  VCC: Nokia_5110_LCD_Module1.Vcc, U1.VCC, U1.CH_PD, GY-NEO6MV3.VCC, Gyroscope.VCC, VCC1.+
  GND: Nokia_5110_LCD_Module1.Grnd, U1.GND, GY-NEO6MV3.GND, Gyroscope.GND, VCC1.-
  N1: Nokia_5110_LCD_Module1.SCE, Composant2.D11_PWM/MOSI
  N2: Nokia_5110_LCD_Module1.RST, Composant2.D10_PWM/SS
  N3: Nokia_5110_LCD_Module1.D/C, Composant2.D9_PWM
  N4: Nokia_5110_LCD_Module1.6_DN_(MOSI), Composant2.D8
  N5: Nokia_5110_LCD_Module1.SCLK, Composant2.D7
  N6: Nokia_5110_LCD_Module1.LED, Composant2.D6_PWM
  N7: U1.RXD, Composant2.D0/RX
  N8: U1.TXD, Composant2.D1/TX
  N9: GY-NEO6MV3.RX-I, Composant2.D3_PWM
  N10: GY-NEO6MV3.TX-O, Composant2.D2
  N11: Gyroscope.YOUT, Composant2.D5_PWM
  N12: Gyroscope.XOUT, Composant2.D4

custom parts:
  : Nokia 5110 LCD with 8 pin. It's a 45mm*45mm module part. Description: The Nokia 5110 is a basic graphic LCD screen for lots of applications. It was originally intended for as a cell phone screen. This one is mounted on an easy to solder PCB. It uses the PCD8544 controller. The PCD8544 is a low power CMOS LCD controller/driver, designed to drive a graphic display of 48 rows and 84 columns. All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
  ESP8266 WiFi Module: Generic WiFi Module based on the ESP8266 with onboard PCB antenna and UART communications
